// Logisim project boardlib.circ as structural Verilog
module board_interface (
  input  [31:0] _0x3018,
  input  [31:0] _0x3014,
  input  [31:0] _0x3010,
  input  [31:0] _0x300C,
  input  [31:0] _0x3008,
  input  [31:0] _0x3004,
  input  [5:0] row1,
  input  [5:0] row2,
  input  clk,
  output [16:0] _0x3018_2,
  output [9:0] _0x3014_2,
  output [9:0] _0x3010_2,
  output [9:0] _0x300C_2,
  output [9:0] _0x3008_2,
  output [9:0] _0x3004_2,
  output [31:0] _0x3000,
  output irq
);

  wire not_1_out, or_1_out, or_2_out, or_3_out, or_4_out, or_5_out, or_6_out, or_7_out;

  or or_1 (or_1_out, row1[0], row1[1], row1[2], row1[3], row1[4]);
  or or_2 (or_2_out, row2[0], row2[1], row2[2], row2[3], row2[4]);
  Register #(.width(16)) register_1 (
    .D({4'b0000, row2, row1}), .en(not_1_out), .Q(_0x3000[15:0]), .clk(clk), .clr(or_3_out));
  or or_3 (or_3_out, _0x3018[18], ~_0x3018[17]);  // OR_Gate
  or or_4 (or_4_out, or_1_out, or_2_out);
  not not_1 (not_1_out, or_6_out);
  or or_5 (or_5_out, or_4_out, row1[5], row2[5]);
  or or_6 (or_6_out, _0x3000[0], _0x3000[1], _0x3000[2], _0x3000[3], _0x3000[4], _0x3000[5], _0x3000[6], _0x3000[7], _0x3000[8], _0x3000[9], _0x3000[10], _0x3000[11]);
  or or_7 (or_7_out, or_6_out, or_5_out);
  and and_1 (irq, or_7_out, _0x3018[17]);

  assign _0x300C_2 = _0x300C[9:0];
  assign _0x3000[31:16] = {16{1'b0}};
  assign _0x3004_2 = _0x3004[9:0];
  assign _0x3008_2 = _0x3008[9:0];
  assign _0x3010_2 = _0x3010[9:0];
  assign _0x3014_2 = _0x3014[9:0];
  assign _0x3018_2 = _0x3018[16:0];
  // also tied to GND on the sheet: {_0x300C[10], _0x300C[11], _0x300C[12], _0x300C[13], _0x300C[14], _0x300C[15], _0x300C[16], _0x300C[17], _0x300C[18], _0x300C[19], _0x300C[20], _0x300C[21], _0x300C[22], _0x300C[23], _0x300C[24], _0x300C[25], _0x300C[26], _0x300C[27], _0x300C[28], _0x300C[29], _0x300C[30], _0x300C[31], _0x3004[10], _0x3004[11], _0x3004[12], _0x3004[13], _0x3004[14], _0x3004[15], _0x3004[16], _0x3004[17], _0x3004[18], _0x3004[19], _0x3004[20], _0x3004[21], _0x3004[22], _0x3004[23], _0x3004[24], _0x3004[25], _0x3004[26], _0x3004[27], _0x3004[28], _0x3004[29], _0x3004[30], _0x3004[31], _0x3008[10], _0x3008[11], _0x3008[12], _0x3008[13], _0x3008[14], _0x3008[15], _0x3008[16], _0x3008[17], _0x3008[18], _0x3008[19], _0x3008[20], _0x3008[21], _0x3008[22], _0x3008[23], _0x3008[24], _0x3008[25], _0x3008[26], _0x3008[27], _0x3008[28], _0x3008[29], _0x3008[30], _0x3008[31], _0x3010[10], _0x3010[11], _0x3010[12], _0x3010[13], _0x3010[14], _0x3010[15], _0x3010[16], _0x3010[17], _0x3010[18], _0x3010[19], _0x3010[20], _0x3010[21], _0x3010[22], _0x3010[23], _0x3010[24], _0x3010[25], _0x3010[26], _0x3010[27], _0x3010[28], _0x3010[29], _0x3010[30], _0x3010[31], _0x3014[10], _0x3014[11], _0x3014[12], _0x3014[13], _0x3014[14], _0x3014[15], _0x3014[16], _0x3014[17], _0x3014[18], _0x3014[19], _0x3014[20], _0x3014[21], _0x3014[22], _0x3014[23], _0x3014[24], _0x3014[25], _0x3014[26], _0x3014[27], _0x3014[28], _0x3014[29], _0x3014[30], _0x3014[31]}

  // Other names for the same wires on the sheet: redbuttons[4:0] = row1[4:0]; clr = row1[5];
  //   yellowbuttons[4:0] = row2[4:0]; new = row2[5]; display[16:0] = _0x3018[16:0]; intr_en = _0x3018[17];
  //   int_clr = _0x3018[18]

  // Notes on the sheet:
  //   Register 0x3000
  //   <0:4> - r buttons
  //   <5> - Continue
  //   <6:10> - y buttons
  //   <11> - New
endmodule

module slots_interface (
  input  [9:0] \input ,
  output [9:0] input_2,
  output b1,
  output b0
);

  and and_1 (b1, \input [1], ~\input [0]);  // AND_Gate
  and and_2 (b0, \input [0], ~\input [1]);  // AND_Gate

  assign input_2 = {2'b00, \input [9:2]};

  // Notes on the sheet:
  //   gets first 2 bits for LED (R and Y) then sends the remaining 8 bits to next stage
endmodule

module score_interface (
  input  [16:0] IN,
  output Top1,
  output out_3,
  output out_4,
  output out_5,
  output Bottom1,
  output out_7,
  output out_8,
  output out_9,
  output Top2,
  output out_11,
  output out_12,
  output out_13,
  output Bottom2,
  output out_15,
  output out_16,
  output out_17
);

  Multiplexer #(.width(16), .disabled(0), .enable("false")) multiplexer_1 (
    .in0({16{1'b0}}), .in1(IN[15:0]),
    .out({out_17, Top2, out_11, Bottom2, out_15, out_16, out_13, out_12, out_9, Top1, out_3, Bottom1, out_7, out_8, out_5, out_4}),
    .sel(IN[16]));
endmodule

module buttons_interconn (
  input  _0,
  input  _1,
  input  _2,
  input  _3,
  input  _4,
  input  _5,
  output [5:0] out
);


  assign out = {_5, _4, _3, _2, _1, _0};
endmodule

module wires1 (
  input  [9:0] _0x3014,
  input  [9:0] _0x3010,
  input  [9:0] _0x300C,
  input  [9:0] _0x3008,
  input  [9:0] _0x3004,
  output [9:0] _0x3014_2,
  output [9:0] _0x3010_2,
  output [9:0] _0x300C_2,
  output [9:0] _0x3008_2,
  output [9:0] _0x3004_2
);


  assign _0x300C_2 = _0x300C;
  assign _0x3004_2 = _0x3004;
  assign _0x3008_2 = _0x3008;
  assign _0x3010_2 = _0x3010;
  assign _0x3014_2 = _0x3014;
endmodule
