// Logisim project memory.circ as structural Verilog: 3 circuits, main circuit memory
module memory (
  input  [31:0] inst_addr,
  input  mem_wr,
  input  [31:0] data_addr,
  input  [31:0] data_wdata,
  input  clk,
  input  rst,
  input  [31:0] _0x3000,
  output [31:0] inst_data,
  output [31:0] _0x3018,
  output [31:0] _0x3014,
  output [31:0] _0x3010,
  output [31:0] _0x300c,
  output [31:0] _0x3008,
  output [31:0] data_rdata,
  output [31:0] _0x3004
);

  instmemory instmemory_1 (.inst_addr(inst_addr), .inst_data(inst_data));
  datamemory datamemory_1 (
    .addr(data_addr), .wdata(data_wdata), .mem_wr(mem_wr), .clk(clk), .rst(rst), .rdata(data_rdata),
    ._0x3018(_0x3018), ._0x3014(_0x3014), ._0x3010(_0x3010), ._0x3000(_0x3000), ._0x300c(_0x300c),
    ._0x3008(_0x3008), ._0x3004(_0x3004));
endmodule

module datamemory (
  input  [31:0] addr,
  input  [31:0] wdata,
  input  mem_wr,
  input  clk,
  input  rst,
  input  [31:0] _0x3000,
  output [31:0] rdata,
  output [31:0] _0x3018,
  output [31:0] _0x3014,
  output [31:0] _0x3010,
  output [31:0] _0x300c,
  output [31:0] _0x3008,
  output [31:0] _0x3004
);

  wire _0x300cen, _0x3000en, _0x3004en, _0x3008en, _0x3010en, _0x3014en, _0x3018en, and_1_out, and_2_out,
       and_3_out, and_4_out, and_5_out, and_6_out, read_mem;
  wire [2:0] priority_encoder_1_out;
  wire [31:0] _0x3000_t, ram_1_data;

  Comparator #(.width(32)) comparator_1 (.a(32'h3018), .b(addr), .eq(_0x3018en));  // open: gt, lt
  Comparator #(.width(32)) comparator_2 (.a(32'h3014), .b(addr), .eq(_0x3014en));  // open: gt, lt
  Comparator #(.width(32)) comparator_3 (.a(32'h3010), .b(addr), .eq(_0x3010en));  // open: gt, lt
  Comparator #(.width(32)) comparator_4 (.a(32'h300c), .b(addr), .eq(_0x300cen));  // open: gt, lt
  Comparator #(.width(32)) comparator_5 (.a(32'h3008), .b(addr), .eq(_0x3008en));  // open: gt, lt
  Comparator #(.width(32)) comparator_6 (.a(32'h3004), .b(addr), .eq(_0x3004en));  // open: gt, lt
  Comparator #(.width(32)) comparator_7 (.a(32'h3000), .b(addr), .eq(_0x3000en));  // open: gt, lt
  and and_1 (and_1_out, mem_wr, _0x3018en);
  and and_2 (and_2_out, mem_wr, _0x3014en);
  and and_3 (and_3_out, mem_wr, _0x3010en);
  and and_4 (and_4_out, mem_wr, _0x300cen);
  and and_5 (and_5_out, mem_wr, _0x3008en);
  and and_6 (and_6_out, mem_wr, _0x3004en);
  RAM #(.addrWidth(12), .dataWidth(32), .bus("separate")) ram_1 (
    .addr(addr[13:2]), .din(wdata), .data(ram_1_data), .str(mem_wr), .sel(1'b1), .clk(clk), .ld(1'b1),
    .clr(rst));
  Register #(.width(32)) register_1 (.D(wdata), .en(and_1_out), .Q(_0x3018), .clk(clk), .clr(rst));
  Register #(.width(32)) register_2 (.D(wdata), .en(and_2_out), .Q(_0x3014), .clk(clk), .clr(rst));
  Register #(.width(32)) register_3 (.D(wdata), .en(and_3_out), .Q(_0x3010), .clk(clk), .clr(rst));
  Register #(.width(32)) register_4 (.D(wdata), .en(and_4_out), .Q(_0x300c), .clk(clk), .clr(rst));
  Register #(.width(32)) register_5 (.D(wdata), .en(and_5_out), .Q(_0x3008), .clk(clk), .clr(rst));
  Register #(.width(32)) register_6 (.D(wdata), .en(and_6_out), .Q(_0x3004), .clk(clk), .clr(rst));
  Register #(.width(32)) register_7 (.D(_0x3000), .en(_0x3018[17]), .Q(_0x3000_t), .clk(clk), .clr(rst));
  Multiplexer #(.select(3), .width(32), .disabled(0), .enable("false")) multiplexer_1 (
    .in0(ram_1_data), .in1(_0x3000_t), .in2(_0x3004), .in3(_0x3008), .in4(_0x300c), .in5(_0x3010),
    .in6(_0x3014), .in7(_0x3018), .out(rdata), .sel(priority_encoder_1_out));
  Priority_Encoder priority_encoder_1 (
    .in0(read_mem), .in1(_0x3000en), .in2(_0x3004en), .in3(_0x3008en), .in4(_0x300cen), .in5(_0x3010en),
    .in6(_0x3014en), .in7(_0x3018en), .out(priority_encoder_1_out), .en_in(1'b1));  // open: gs, en_out
  nor nor_1 (read_mem, _0x3000en, _0x3004en, _0x3008en, _0x300cen, _0x3010en, _0x3014en, _0x3018en);

  // Notes on the sheet:
  //   DATA MEM (0x2000-0x2FFC)
endmodule

module instmemory (
  input  [31:0] inst_addr,
  output [31:0] inst_data
);

  wire [31:0] rom_1_data, rom_2_data;

  ROM #(.addrWidth(10), .dataWidth(32)) rom_1 (.addr(inst_addr[11:2]), .data(rom_1_data), .sel(1'b1));
  ROM #(.addrWidth(10), .dataWidth(32)) rom_2 (.addr(inst_addr[11:2]), .data(rom_2_data), .sel(1'b1));
  Multiplexer #(.width(32), .disabled(0), .enable("false")) multiplexer_1 (
    .in0(rom_1_data), .in1(rom_2_data), .out(inst_data), .sel(inst_addr[12]));

  // Notes on the sheet:
  //   MAIN INST MEM (0x0000-0x0FFC)
  //   ISR INST MEM (0x1000-0x1FFC)
  //   contents of rom_1 (hex, n*v repeats v):
  //   20083000 ad000000 ad000004 ad000008 ad00000c ad000010 ad000014 20090001 92c00 93440 92480 a64820
  //   ad090018 1084022 1000ffff
  //   contents of rom_2 (hex, n*v repeats v):
  //   20083000 8d0a0000 1084022 a5042 11400002 21080001 1000fffc 100b820 14a5022 200a0005 11480004 14a5022
  //   200a000b 11480009 10000012 1294822 20093000 ad200004 ad200008 ad20000c ad200010 ad200014 10000143
  //   1294822 20093000 ad200004 ad200008 ad20000c ad200010 ad200014 a66020 ad2c0018 10000139 1294822 84820
  //   11200009 2129ffff 11200007 2129ffff 11200005 2129ffff 11200003 2129ffff 11200001 1000001e 1294822
  //   200b0005 20093000 14a5022 11600128 200e001e 21290004 8d2c0000 200a0008 108c020 1585022 1ca7022 ed020
  //   1807820 f7840 235affff 1740fffd f7f82 216bffff 15e0fff0 201b0001 214a0001 1ce7022 100a0003 1bd840
  //   21ce0001 15cafffd 19b6020 ad2c0000 1000001e 22f7fffa 1294822 200b0005 20093000 14a5022 11600109
  //   200e001e 21290004 8d2c0000 200a0008 2f7c020 1585022 1ca7022 ed020 1807820 f7840 235affff 1740fffd
  //   f7f82 216bffff 15e0fff0 201b0001 1ce7022 100affe5 1bd840 21ce0001 15cafffd 19b6020 ad2c0000 10000070
  //   1084022 1294822 14a5022 16b5822 18c6022 e73822 2108022 2318822 2529022 2739822 294a022 2b5a822
  //   20083000 20070008 8d080004 8d090008 8d0a000c 8d0b0010 8d0c0014 88202 98a02 a9202 b9a02 ca202 211a820
  //   2b2a820 2b3a820 12a700c4 2b0a822 2b4a820 12a700c1 88600 108782 98e00 118f82 a9600 129782 b9e00
  //   139f82 ca600 14a782 211a820 2b2a820 2b3a820 12a700b3 2b0a822 2b4a820 12a700b0 88680 108782 98e80
  //   118f82 a9680 129782 b9e80 139f82 ca680 14a782 211a820 2b2a820 2b3a820 12a700a2 2b0a822 2b4a820
  //   12a7009f 88700 108782 98f00 118f82 a9700 129782 b9f00 139f82 ca700 14a782 211a820 2b2a820 2b3a820
  //   12a70091 2b0a822 2b4a820 12a7008e 88780 108782 98f80 118f82 a9780 129782 b9f80 139f82 ca780 14a782
  //   211a820 2b2a820 2b3a820 12a70080 2b0a822 2b4a820 12a7007d 20083000 200b00aa 200d0005 21080004
  //   8d090000 95082 114b0076 95600 a5602 114b0073 21adffff 15a0fff7 10000081 1084022 1294822 14a5022
  //   16b5822 18c6022 e73822 2108022 2318822 2529022 2739822 294a022 2b5a822 20083000 20070004 8d080004
  //   8d090008 8d0a000c 8d0b0010 8d0c0014 88202 98a02 a9202 b9a02 ca202 211a820 2b2a820 2b3a820 12a7005d
  //   2b0a822 2b4a820 12a7005a 88600 108782 98e00 118f82 a9600 129782 b9e00 139f82 ca600 14a782 211a820
  //   2b2a820 2b3a820 12a7004c 2b0a822 2b4a820 12a70049 88680 108782 98e80 118f82 a9680 129782 b9e80
  //   139f82 ca680 14a782 211a820 2b2a820 2b3a820 12a7003b 2b0a822 2b4a820 12a70038 88700 108782 98f00
  //   118f82 a9700 129782 b9f00 139f82 ca700 14a782 211a820 2b2a820 2b3a820 12a7002a 2b0a822 2b4a820
  //   12a70027 88780 108782 98f80 118f82 a9780 129782 b9f80 139f82 ca780 14a782 211a820 2b2a820 2b3a820
  //   12a70019 2b0a822 2b4a820 12a70016 20083000 200b0055 200d0005 21080004 8d090000 95082 114b000f 95600
  //   a5602 114b000c 21adffff 15a0fff7 10000011 1084022 20083018 8d090000 14a5022 200a0001 a5200 12a4820
  //   ad090000 10000008 1084022 20083018 8d090000 14a5022 200a0001 12a4820 ad090000 10000000 1294822
  //   20093018 8d220000 441020 ad220000 441022 ad220000 42000018
endmodule
