// Logisim project mp2_library.circ as structural Verilog: 3 circuits, main circuit MEMORY
module REG_FILE (
  input  [31:0] wr_data,
  input  clk,
  input  rst,
  input  [4:0] rd_reg1,
  input  wr_en,
  input  [4:0] wr_reg,
  input  [4:0] rd_reg2,
  output [31:0] rd_data1,
  output [31:0] rd_data2
);

  wire W00, W01, W02, W03, W04, W05, W06, W07, W08, W09, W10, W11, W12, W13, W14, W15, W16, W17, W18, W19,
       W20, W21, W22, W23, W24, W25, W26, W27, W28, W29, W30, W31;
  wire [31:0] Q01, Q02, Q03, Q04, Q05, Q06, Q07, Q08, Q09, Q10, Q11, Q12, Q13, Q14, Q15, Q16, Q17, Q18, Q19,
       Q20, Q21, Q22, Q23, Q24, Q25, Q26, Q27, Q28, Q29, Q30, Q31;

  Demultiplexer #(.select(5), .disabled(0)) demultiplexer_1 (
    .out0(W00), .out1(W01), .out2(W02), .out3(W03), .out4(W04), .out5(W05), .out6(W06), .out7(W07),
    .out8(W08), .out9(W09), .out10(W10), .out11(W11), .out12(W12), .out13(W13), .out14(W14), .out15(W15),
    .out16(W16), .out17(W17), .out18(W18), .out19(W19), .out20(W20), .out21(W21), .out22(W22), .out23(W23),
    .out24(W24), .out25(W25), .out26(W26), .out27(W27), .out28(W28), .out29(W29), .out30(W30), .out31(W31),
    .in(1'b1), .sel(wr_reg), .en(wr_en));
  Register #(.width(32)) register_1 (.D(wr_data), .en(W01), .Q(Q01), .clk(clk), .clr(rst));
  Register #(.width(32)) register_2 (.D(wr_data), .en(W02), .Q(Q02), .clk(clk), .clr(rst));
  Register #(.width(32)) register_3 (.D(wr_data), .en(W03), .Q(Q03), .clk(clk), .clr(rst));
  Register #(.width(32)) register_4 (.D(wr_data), .en(W04), .Q(Q04), .clk(clk), .clr(rst));
  Register #(.width(32)) register_5 (.D(wr_data), .en(W05), .Q(Q05), .clk(clk), .clr(rst));
  Register #(.width(32)) register_6 (.D(wr_data), .en(W06), .Q(Q06), .clk(clk), .clr(rst));
  Register #(.width(32)) register_7 (.D(wr_data), .en(W07), .Q(Q07), .clk(clk), .clr(rst));
  Register #(.width(32)) register_8 (.D(wr_data), .en(W08), .Q(Q08), .clk(clk), .clr(rst));
  Register #(.width(32)) register_9 (.D(wr_data), .en(W09), .Q(Q09), .clk(clk), .clr(rst));
  Register #(.width(32)) register_10 (.D(wr_data), .en(W10), .Q(Q10), .clk(clk), .clr(rst));
  Register #(.width(32)) register_11 (.D(wr_data), .en(W11), .Q(Q11), .clk(clk), .clr(rst));
  Register #(.width(32)) register_12 (.D(wr_data), .en(W12), .Q(Q12), .clk(clk), .clr(rst));
  Register #(.width(32)) register_13 (.D(wr_data), .en(W13), .Q(Q13), .clk(clk), .clr(rst));
  Register #(.width(32)) register_14 (.D(wr_data), .en(W14), .Q(Q14), .clk(clk), .clr(rst));
  Register #(.width(32)) register_15 (.D(wr_data), .en(W15), .Q(Q15), .clk(clk), .clr(rst));
  Register #(.width(32)) register_16 (.D(wr_data), .en(W16), .Q(Q16), .clk(clk), .clr(rst));
  Register #(.width(32)) register_17 (.D(wr_data), .en(W17), .Q(Q17), .clk(clk), .clr(rst));
  Register #(.width(32)) register_18 (.D(wr_data), .en(W18), .Q(Q18), .clk(clk), .clr(rst));
  Register #(.width(32)) register_19 (.D(wr_data), .en(W19), .Q(Q19), .clk(clk), .clr(rst));
  Register #(.width(32)) register_20 (.D(wr_data), .en(W20), .Q(Q20), .clk(clk), .clr(rst));
  Register #(.width(32)) register_21 (.D(wr_data), .en(W21), .Q(Q21), .clk(clk), .clr(rst));
  Register #(.width(32)) register_22 (.D(wr_data), .en(W22), .Q(Q22), .clk(clk), .clr(rst));
  Register #(.width(32)) register_23 (.D(wr_data), .en(W23), .Q(Q23), .clk(clk), .clr(rst));
  Register #(.width(32)) register_24 (.D(wr_data), .en(W24), .Q(Q24), .clk(clk), .clr(rst));
  Register #(.width(32)) register_25 (.D(wr_data), .en(W25), .Q(Q25), .clk(clk), .clr(rst));
  Register #(.width(32)) register_26 (.D(wr_data), .en(W26), .Q(Q26), .clk(clk), .clr(rst));
  Register #(.width(32)) register_27 (.D(wr_data), .en(W27), .Q(Q27), .clk(clk), .clr(rst));
  Register #(.width(32)) register_28 (.D(wr_data), .en(W28), .Q(Q28), .clk(clk), .clr(rst));
  Register #(.width(32)) register_29 (.D(wr_data), .en(W29), .Q(Q29), .clk(clk), .clr(rst));
  Register #(.width(32)) register_30 (.D(wr_data), .en(W30), .Q(Q30), .clk(clk), .clr(rst));
  Register #(.width(32)) register_31 (.D(wr_data), .en(W31), .Q(Q31), .clk(clk), .clr(rst));
  Multiplexer #(.select(5), .width(32), .disabled(0), .enable("false")) multiplexer_1 (
    .in0({32{1'b0}}), .in1(Q01), .in2(Q02), .in3(Q03), .in4(Q04), .in5(Q05), .in6(Q06), .in7(Q07), .in8(Q08),
    .in9(Q09), .in10(Q10), .in11(Q11), .in12(Q12), .in13(Q13), .in14(Q14), .in15(Q15), .in16(Q16),
    .in17(Q17), .in18(Q18), .in19(Q19), .in20(Q20), .in21(Q21), .in22(Q22), .in23(Q23), .in24(Q24),
    .in25(Q25), .in26(Q26), .in27(Q27), .in28(Q28), .in29(Q29), .in30(Q30), .in31(Q31), .out(rd_data1),
    .sel(rd_reg1));
  Multiplexer #(.select(5), .width(32), .disabled(0), .enable("false")) multiplexer_2 (
    .in0({32{1'b0}}), .in1(Q01), .in2(Q02), .in3(Q03), .in4(Q04), .in5(Q05), .in6(Q06), .in7(Q07), .in8(Q08),
    .in9(Q09), .in10(Q10), .in11(Q11), .in12(Q12), .in13(Q13), .in14(Q14), .in15(Q15), .in16(Q16),
    .in17(Q17), .in18(Q18), .in19(Q19), .in20(Q20), .in21(Q21), .in22(Q22), .in23(Q23), .in24(Q24),
    .in25(Q25), .in26(Q26), .in27(Q27), .in28(Q28), .in29(Q29), .in30(Q30), .in31(Q31), .out(rd_data2),
    .sel(rd_reg2));

  // Other names for the same wires on the sheet: D[31:0] = wr_data
endmodule

module MEMORY (
  input  [31:0] write_data,
  input  mem_wr,
  input  clk,
  input  rst,
  input  [31:0] addr,
  output [31:0] mem_data
);

  wire comparator_1_lt;
  wire [31:0] multiplexer_1_out, ram_1_data, rom_1_data, rom_2_data;

  RAM #(.addrWidth(12), .dataWidth(32), .bus("separate")) ram_1 (
    .addr(addr[13:2]), .din(write_data), .data(ram_1_data), .str(mem_wr), .sel(1'b1), .clk(clk), .ld(1'b1),
    .clr(rst));
  ROM #(.addrWidth(10), .dataWidth(32)) rom_1 (.addr(addr[11:2]), .data(rom_1_data), .sel(1'b1));
  ROM #(.addrWidth(10), .dataWidth(32)) rom_2 (.addr(addr[11:2]), .data(rom_2_data), .sel(1'b1));
  Comparator #(.width(32)) comparator_1 (.a(addr), .b(32'h2000), .lt(comparator_1_lt));  // open: gt, eq
  Multiplexer #(.width(32), .disabled(0), .enable("false")) multiplexer_1 (
    .in0(rom_1_data), .in1(rom_2_data), .out(multiplexer_1_out), .sel(addr[12]));
  Multiplexer #(.width(32), .disabled(0), .enable("false")) multiplexer_2 (
    .in0(ram_1_data), .in1(multiplexer_1_out), .out(mem_data), .sel(comparator_1_lt));

  // Notes on the sheet:
  //   DATA MEM (0x0000-0x3000)
  //   but only (0x2000-0x3000) is usable
  //   MAIN INST MEM (0x0000-0x0FFC)
  //   ISR INST MEM (0x1000-0x1FFC)
  //   contents of rom_1 (hex, n*v repeats v):
  //   20083000 ad000000 ad000004 ad000008 ad00000c ad000010 ad000014 20090001 92c00 93440 92480 a64820
  //   ad090018 1084022 1000ffff
  //   contents of rom_2 (hex, n*v repeats v):
  //   20083000 8d0a0000 1084022 a5042 11400002 21080001 1000fffc 100b820 14a5022 200a0005 11480004 14a5022
  //   200a000b 11480009 10000012 1294822 20093000 ad200004 ad200008 ad20000c ad200010 ad200014 10000143
  //   1294822 20093000 ad200004 ad200008 ad20000c ad200010 ad200014 a66020 ad2c0018 10000139 1294822 84820
  //   11200009 2129ffff 11200007 2129ffff 11200005 2129ffff 11200003 2129ffff 11200001 1000001e 1294822
  //   200b0005 20093000 14a5022 11600128 200e001e 21290004 8d2c0000 200a0008 108c020 1585022 1ca7022 ed020
  //   1807820 f7840 235affff 1740fffd f7f82 216bffff 15e0fff0 201b0001 214a0001 1ce7022 100a0003 1bd840
  //   21ce0001 15cafffd 19b6020 ad2c0000 1000001e 22f7fffa 1294822 200b0005 20093000 14a5022 11600109
  //   200e001e 21290004 8d2c0000 200a0008 2f7c020 1585022 1ca7022 ed020 1807820 f7840 235affff 1740fffd
  //   f7f82 216bffff 15e0fff0 201b0001 1ce7022 100affe5 1bd840 21ce0001 15cafffd 19b6020 ad2c0000 10000070
  //   1084022 1294822 14a5022 16b5822 18c6022 e73822 2108022 2318822 2529022 2739822 294a022 2b5a822
  //   20083000 20070008 8d080004 8d090008 8d0a000c 8d0b0010 8d0c0014 88202 98a02 a9202 b9a02 ca202 211a820
  //   2b2a820 2b3a820 12a700c4 2b0a822 2b4a820 12a700c1 88600 108782 98e00 118f82 a9600 129782 b9e00
  //   139f82 ca600 14a782 211a820 2b2a820 2b3a820 12a700b3 2b0a822 2b4a820 12a700b0 88680 108782 98e80
  //   118f82 a9680 129782 b9e80 139f82 ca680 14a782 211a820 2b2a820 2b3a820 12a700a2 2b0a822 2b4a820
  //   12a7009f 88700 108782 98f00 118f82 a9700 129782 b9f00 139f82 ca700 14a782 211a820 2b2a820 2b3a820
  //   12a70091 2b0a822 2b4a820 12a7008e 88780 108782 98f80 118f82 a9780 129782 b9f80 139f82 ca780 14a782
  //   211a820 2b2a820 2b3a820 12a70080 2b0a822 2b4a820 12a7007d 20083000 200b00aa 200d0005 21080004
  //   8d090000 95082 114b0076 95600 a5602 114b0073 21adffff 15a0fff7 10000081 1084022 1294822 14a5022
  //   16b5822 18c6022 e73822 2108022 2318822 2529022 2739822 294a022 2b5a822 20083000 20070004 8d080004
  //   8d090008 8d0a000c 8d0b0010 8d0c0014 88202 98a02 a9202 b9a02 ca202 211a820 2b2a820 2b3a820 12a7005d
  //   2b0a822 2b4a820 12a7005a 88600 108782 98e00 118f82 a9600 129782 b9e00 139f82 ca600 14a782 211a820
  //   2b2a820 2b3a820 12a7004c 2b0a822 2b4a820 12a70049 88680 108782 98e80 118f82 a9680 129782 b9e80
  //   139f82 ca680 14a782 211a820 2b2a820 2b3a820 12a7003b 2b0a822 2b4a820 12a70038 88700 108782 98f00
  //   118f82 a9700 129782 b9f00 139f82 ca700 14a782 211a820 2b2a820 2b3a820 12a7002a 2b0a822 2b4a820
  //   12a70027 88780 108782 98f80 118f82 a9780 129782 b9f80 139f82 ca780 14a782 211a820 2b2a820 2b3a820
  //   12a70019 2b0a822 2b4a820 12a70016 20083000 200b0055 200d0005 21080004 8d090000 95082 114b000f 95600
  //   a5602 114b000c 21adffff 15a0fff7 10000011 1084022 20083018 8d090000 14a5022 200a0001 a5200 12a4820
  //   ad090000 10000008 1084022 20083018 8d090000 14a5022 200a0001 12a4820 ad090000 10000000 1294822
  //   20093018 8d220000 441020 ad220000 441022 ad220000 42000018
endmodule

module ALU (
  input  [31:0] imm,
  input  [4:0] shamt,
  input  [31:0] op1,
  input  [31:0] op2,
  input  [5:0] ALU_code,
  output zero_flag,
  output [31:0] result
);

  wire comparator_1_lt, comparator_2_lt, comparator_3_eq, comparator_4_gt, comparator_4_lt, funct_add,
       funct_addi, funct_and, funct_andi, funct_beq, funct_bne, funct_lw, funct_nor, funct_or, funct_ori,
       funct_sel_en, funct_sll, funct_sllv, funct_slt, funct_slti, funct_srl, funct_srlv, funct_sub,
       funct_sw, funct_xor, funct_xori, or_3_out, or_4_out, or_5_out;
  wire [4:0] funct_sel;
  wire [31:0] res_add, res_addi, res_and, res_andi, res_beq, res_bne, res_nor, res_or, res_ori, res_sll,
       res_sllv, res_slt, res_slti, res_srl, res_srlv, res_sub, res_xor, res_xori, subtractor_2_out,
       subtractor_3_out;

  Adder #(.width(32)) adder_1 (.a(op1), .b(op2), .out(res_add));  // open: cin, cout
  Subtractor #(.width(32)) subtractor_1 (.a(op1), .b(op2), .out(res_sub));  // open: bin, bout
  assign res_and = op1 & op2;  // AND_Gate and_1, 32 bits wide
  assign res_or = op1 | op2;  // OR_Gate or_1, 32 bits wide
  assign res_nor = ~(op1 | op2);  // NOR_Gate nor_1, 32 bits wide
  assign res_xor = op1 ^ op2;  // XOR_Gate xor_1, 32 bits wide
  Adder #(.width(32)) adder_2 (.a(op1), .b(imm), .out(res_addi));  // open: cin, cout
  assign res_andi = op1 & imm;  // AND_Gate and_2, 32 bits wide
  assign res_ori = op1 | imm;  // OR_Gate or_2, 32 bits wide
  Shifter #(.width(32)) shifter_1 (.in(op2), .\dist (shamt), .out(res_sll));
  Shifter #(.width(32), .shift("lr")) shifter_2 (.in(op2), .\dist (shamt), .out(res_srl));
  assign res_xori = op1 ^ imm;  // XOR_Gate xor_2, 32 bits wide
  Comparator #(.width(32)) comparator_1 (.a(op1), .b(op2), .lt(comparator_1_lt));  // open: gt, eq
  Comparator #(.width(32)) comparator_2 (.a(op1), .b(imm), .lt(comparator_2_lt));  // open: gt, eq
  Subtractor #(.width(32)) subtractor_2 (.a(op1), .b(op2), .out(subtractor_2_out));  // open: bin, bout
  // Probe on subtractor_3_out
  Subtractor #(.width(32)) subtractor_3 (.a(op1), .b(op2), .out(subtractor_3_out));  // open: bin, bout
  // Probe on op1[4:0]
  assign res_slt = {{31{1'b0}}, or_3_out};  // Bit_Extender bit_extender_1
  or or_3 (or_3_out, comparator_1_lt, 1'b0);
  assign res_slti = {{31{1'b0}}, or_4_out};  // Bit_Extender bit_extender_2
  or or_4 (or_4_out, comparator_2_lt, 1'b0);
  // Probe on comparator_3_eq
  Comparator #(.width(32)) comparator_3 (.a(subtractor_2_out), .b({32{1'b0}}), .eq(comparator_3_eq));  // open: gt, lt
  Comparator #(.width(32)) comparator_4 (
    .a(subtractor_3_out), .b({32{1'b0}}), .gt(comparator_4_gt), .lt(comparator_4_lt));  // open: eq
  or or_5 (or_5_out, comparator_4_gt, comparator_4_lt);
  // Probe on res_add
  // Probe on res_sub
  // Probe on res_addi
  // Probe on op1
  assign res_beq = {{31{1'b0}}, comparator_3_eq};  // Bit_Extender bit_extender_3
  // Probe on or_5_out
  assign res_bne = {{31{or_5_out}}, or_5_out};  // Bit_Extender bit_extender_4
  // Probe on op2
  Shifter #(.width(32)) shifter_3 (.in(op2), .\dist (op1[4:0]), .out(res_sllv));
  Shifter #(.width(32), .shift("lr")) shifter_4 (.in(op2), .\dist (op1[4:0]), .out(res_srlv));
  // Probe on op2
  // Probe on res_sllv
  Comparator #(.width(6)) comparator_5 (.a(ALU_code), .b(6'b100000), .eq(funct_add));  // open: gt, lt
  Comparator #(.width(6)) comparator_6 (.a(ALU_code), .b(6'b100010), .eq(funct_sub));  // open: gt, lt
  Comparator #(.width(6)) comparator_7 (.a(ALU_code), .b(6'b100100), .eq(funct_and));  // open: gt, lt
  Comparator #(.width(6)) comparator_8 (.a(ALU_code), .b(6'b100101), .eq(funct_or));  // open: gt, lt
  Comparator #(.width(6)) comparator_9 (.a(ALU_code), .b(6'b100111), .eq(funct_nor));  // open: gt, lt
  Comparator #(.width(6)) comparator_10 (.a(ALU_code), .b(6'b100110), .eq(funct_xor));  // open: gt, lt
  Comparator #(.width(6)) comparator_11 (.a(ALU_code), .b(6'b101010), .eq(funct_slt));  // open: gt, lt
  Comparator #(.width(6)) comparator_12 (.a(ALU_code), .b({6{1'b0}}), .eq(funct_sll));  // open: gt, lt
  Comparator #(.width(6)) comparator_13 (.a(ALU_code), .b(6'b000010), .eq(funct_srl));  // open: gt, lt
  Comparator #(.width(6)) comparator_14 (.a(ALU_code), .b(6'b001000), .eq(funct_addi));  // open: gt, lt
  Comparator #(.width(6)) comparator_15 (.a(ALU_code), .b(6'b001010), .eq(funct_slti));  // open: gt, lt
  Comparator #(.width(6)) comparator_16 (.a(ALU_code), .b(6'b001100), .eq(funct_andi));  // open: gt, lt
  Comparator #(.width(6)) comparator_17 (.a(ALU_code), .b(6'b001101), .eq(funct_ori));  // open: gt, lt
  Comparator #(.width(6)) comparator_18 (.a(ALU_code), .b(6'b001110), .eq(funct_xori));  // open: gt, lt
  Comparator #(.width(6)) comparator_19 (.a(ALU_code), .b(6'b000100), .eq(funct_beq));  // open: gt, lt
  Comparator #(.width(6)) comparator_20 (.a(ALU_code), .b(6'b000101), .eq(funct_bne));  // open: gt, lt
  Comparator #(.width(6)) comparator_21 (.a(ALU_code), .b(6'b101011), .eq(funct_sw));  // open: gt, lt
  Comparator #(.width(6)) comparator_22 (.a(ALU_code), .b(6'b100011), .eq(funct_lw));  // open: gt, lt
  Comparator #(.width(6)) comparator_23 (.a(ALU_code), .b(6'b000110), .eq(funct_srlv));  // open: gt, lt
  Comparator #(.width(6)) comparator_24 (.a(ALU_code), .b(6'b000100), .eq(funct_sllv));  // open: gt, lt
  Multiplexer #(.select(5), .width(32)) multiplexer_1 (
    .in0(res_add), .in1(res_sub), .in2(res_and), .in3(res_or), .in4(res_nor), .in5(res_xor), .in6(res_slt),
    .in7(res_sll), .in8(res_srl), .in9(res_addi), .in10(res_slti), .in11(res_andi), .in12(res_ori),
    .in13(res_xori), .in14(res_beq), .in15(res_bne), .in16(res_add), .in17(res_add), .in18(res_srlv),
    .in19(res_sllv), .out(result), .sel(funct_sel), .en(funct_sel_en));  // open: in20, in21, in22, in23, in24, in25, in26, in27, in28, in29, in30, in31
  Comparator #(.width(32)) comparator_25 (.a(result), .b({32{1'b0}}), .eq(zero_flag));  // open: gt, lt
  Priority_Encoder #(.select(5)) priority_encoder_1 (
    .in0(funct_add), .in1(funct_sub), .in2(funct_and), .in3(funct_or), .in4(funct_nor), .in5(funct_xor),
    .in6(funct_slt), .in7(funct_sll), .in8(funct_srl), .in9(funct_addi), .in10(funct_slti),
    .in11(funct_andi), .in12(funct_ori), .in13(funct_xori), .in14(funct_beq), .in15(funct_bne),
    .in16(funct_sw), .in17(funct_lw), .in18(funct_srlv), .in19(funct_sllv), .out(funct_sel),
    .gs(funct_sel_en), .en_in(1'b1));  // open: in20, in21, in22, in23, in24, in25, in26, in27, in28, in29, in30, in31, en_out

  // Other names for the same wires on the sheet: res_lw[31:0] = res_add; res_sw[31:0] = res_add

  // Notes on the sheet:
  //   Results 
endmodule
