// Logisim project mp2_mendaros.circ as structural Verilog: 1 circuit, main circuit main
module main (
  input  clk,
  input  rst,
  input  [31:0] inst_data,
  input  interrupt__from_device,
  input  [31:0] read_data,
  output [31:0] inst_addr,
  output mem_wr,
  output [31:0] write_data,
  output [31:0] data_addr,
  output [31:0] PC,
  output [31:0] ALU_OUT
);

  wire and_1_out, and_2_out, and_3_out, and_4_out, and_5_out, and_6_out, and_7_out, and_8_out, and_9_out,
       and_10_out, and_11_out, and_12_out, and_13_out, and_14_out, and_15_out, and_16_out, and_17_out,
       and_19_out, and_21_out, and_22_out, and_25_out, and_26_out, and_27_out, and_28_out, and_29_out,
       and_30_out, and_31_out, and_32_out, arithmetic, bitwise_imm, branched, comparator_1_eq,
       comparator_2_eq, comparator_3_eq, comparator_4_eq, comparator_5_eq, comparator_6_eq, comparator_7_eq,
       comparator_8_eq, comparator_9_eq, comparator_10_eq, comparator_11_eq, comparator_12_eq,
       comparator_13_eq, comparator_14_eq, comparator_15_eq, comparator_16_eq, comparator_17_eq,
       comparator_18_eq, comparator_19_eq, comparator_20_eq, comparator_21_eq, comparator_22_eq,
       comparator_23_eq, comparator_24_eq, comparator_25_eq, comparator_26_eq, comparator_27_eq,
       comparator_28_eq, comparator_31_eq, comparator_32_eq, comparator_33_eq, comparator_34_eq,
       comparator_35_eq, comparator_36_eq, comparator_37_eq, comparator_38_eq, comparator_39_eq,
       comparator_40_eq, comparator_41_eq, comparator_42_eq, comparator_42_gt, comparator_44_eq,
       comparator_45_eq, comparator_45_lt, enable_int, ERET, i_type, int_signal, is_itype, j_type, jal, jr,
       jump, mp2board, multiplexer_5_out, NOP, not_1_out, not_2_out, not_3_out, not_4_out, not_5_out,
       not_6_out, not_7_out, not_8_out, not_9_out, not_10_out, not_11_out, or_1_out, or_3_out, or_4_out,
       or_5_out, or_8_out, or_9_out, or_11_out, or_12_out, or_13_out, or_15_out, or_18_out, or_20_out,
       or_22_out, or_23_out, or_24_out, or_25_out, r_type, sel_IorD, sel_isr, sel_opA, stateA, stateB,
       stateC, stateD, stateE, stateF, stateG, stateH, stateI, stateJ, wr_en, wr_en1, wr_pc, zeroflag;
  wire [1:0] priority_encoder_1_out, priority_encoder_2_out, sel_data, sel_dest, sel_PC;
  wire [4:0] _6_10, _11_15, _16_20, _21_25, multiplexer_7_out;
  wire [5:0] _0_5, _31_26, ALU_code, sel_alu;
  wire [27:0] target;
  wire [31:0] A_q, alu_res, bit_extender_1_out, imm_1, imm_final, instruction, MDR_q, multiplexer_4_out,
       multiplexer_10_out, multiplexer_11_out, PC_final, PC_in, rd_data1, reg_file_1_rd_data2, register_1_q,
       shifter_1_out, write_data_t;
  wire [31:28] shifter_2_out;

  // Probe on PC_final
  Multiplexer #(.width(32), .disabled(0), .enable("false")) multiplexer_1 (
    .in0(PC_in), .in1(register_1_q), .out(PC_final), .sel(ERET));
  // Probe on inst_addr
  Multiplexer #(.width(32), .disabled(0), .enable("false")) multiplexer_2 (
    .in0(32'h1000), .in1(PC), .out(inst_addr), .sel(sel_isr));
  Register #(.width(32)) register_1 (.D(PC), .en(int_signal), .Q(register_1_q), .clk(clk), .clr(rst));
  Register #(.width(32)) u_PC (.D(PC_final), .en(wr_pc), .Q(PC), .clk(clk), .clr(rst));
  Multiplexer #(.enable("false")) multiplexer_3 (.in0(1'b0), .in1(1'b1), .out(mem_wr), .sel(comparator_1_eq));
  Comparator #(.width(1)) comparator_1 (.a(stateF), .b(1'b1), .eq(comparator_1_eq));  // open: gt, lt
  // Probe on PC
  Comparator #(.width(6)) comparator_2 (.a(_31_26), .b({6{1'b0}}), .gt(i_type), .eq(comparator_2_eq));  // open: lt
  Comparator #(.width(6)) comparator_3 (.a(ALU_code), .b(6'b001000), .eq(comparator_3_eq));  // open: gt, lt
  Comparator #(.width(6)) comparator_4 (.a(ALU_code), .b(6'b001010), .eq(comparator_4_eq));  // open: gt, lt
  Comparator #(.width(6)) comparator_5 (.a(ALU_code), .b(6'b001100), .eq(comparator_5_eq));  // open: gt, lt
  Comparator #(.width(6)) comparator_6 (.a(ALU_code), .b(6'b001101), .eq(comparator_6_eq));  // open: gt, lt
  Comparator #(.width(6)) comparator_7 (.a(ALU_code), .b(6'b001110), .eq(comparator_7_eq));  // open: gt, lt
  Comparator #(.width(6)) comparator_8 (.a(ALU_code), .b(6'b100011), .eq(comparator_8_eq));  // open: gt, lt
  Comparator #(.width(6)) comparator_9 (.a(ALU_code), .b(6'b101011), .eq(comparator_9_eq));  // open: gt, lt
  // Probe on PC
  Multiplexer #(.width(32), .enable("false")) multiplexer_4 (
    .in0(inst_addr), .in1(ALU_OUT), .out(multiplexer_4_out), .sel(sel_IorD));
  Multiplexer #(.enable("false")) multiplexer_5 (.in0(1'b0), .in1(stateB), .out(multiplexer_5_out), .sel(NOP));
  Comparator #(.width(6)) comparator_10 (.a(ALU_code), .b(6'b101011), .eq(comparator_10_eq));  // open: gt, lt
  Comparator #(.width(6)) comparator_11 (.a(ALU_code), .b(6'b100011), .eq(comparator_11_eq));  // open: gt, lt
  // Probe on instruction
  MEMORY memory_1 (
    .write_data(write_data), .mem_wr(mem_wr), .clk(clk), .rst(rst), .addr(multiplexer_4_out),
    .mem_data(instruction));
  Multiplexer #(.width(32), .enable("false")) multiplexer_6 (
    .in0(imm_1), .in1(bit_extender_1_out), .out(imm_final), .sel(bitwise_imm));
  assign bit_extender_1_out = {{16{1'b0}}, {_11_15, _6_10, _0_5}};  // Bit_Extender bit_extender_1
  // Probe on {_31_26, _21_25, _16_20, _11_15, _6_10, _0_5}
  Register #(.width(32)) IR (
    .D(instruction), .en(stateA), .Q({_31_26, _21_25, _16_20, _11_15, _6_10, _0_5}), .clk(clk), .clr(rst));
  and and_1 (and_1_out, ERET, stateA);
  Register #(.width(32)) MDR (.D(instruction), .en(1'b1), .Q(MDR_q), .clk(clk), .clr(rst));
  or or_1 (or_1_out, stateH, stateD, stateF, stateI, multiplexer_5_out, stateJ, and_1_out);
  or or_2 (arithmetic, comparator_2_eq, comparator_3_eq, comparator_4_eq, comparator_5_eq, comparator_6_eq, comparator_7_eq);
  or or_3 (or_3_out, comparator_8_eq, comparator_9_eq);
  Comparator #(.width(6)) comparator_12 (.a(ALU_code), .b(6'b000100), .eq(comparator_12_eq));  // open: gt, lt
  Comparator #(.width(6)) comparator_13 (.a(ALU_code), .b(6'b000101), .eq(comparator_13_eq));  // open: gt, lt
  // Probe on multiplexer_7_out
  Multiplexer #(.select(2), .width(5), .enable("false")) multiplexer_7 (
    .in0(_16_20), .in1(_11_15), .in2({5{1'b1}}), .out(multiplexer_7_out), .sel(sel_dest));  // open: in3
  Multiplexer #(.width(6), .enable("false")) multiplexer_8 (
    .in0(_31_26), .in1(_0_5), .out(ALU_code), .sel(comparator_14_eq));
  // Probe on write_data_t
  Multiplexer #(.select(2), .width(32), .enable("false")) multiplexer_9 (
    .in0(MDR_q), .in1(ALU_OUT), .in2(PC), .in3(read_data), .out(write_data_t), .sel(sel_data));
  and and_2 (and_2_out, stateB, arithmetic);
  not not_1 (not_1_out, ERET);
  not not_2 (not_2_out, j_type);
  or or_4 (or_4_out, comparator_12_eq, comparator_13_eq);
  // Probe on stateA
  // Probe on stateB
  // Probe on stateC
  // Probe on stateD
  // Probe on stateE
  assign imm_1 = {{16{_11_15[4]}}, {_11_15, _6_10, _0_5}};  // Bit_Extender bit_extender_2
  and and_3 (and_3_out, and_2_out, not_1_out, not_2_out);
  and and_4 (and_4_out, stateB, or_3_out);
  not not_3 (not_3_out, ERET);
  not not_4 (not_4_out, j_type);
  and and_5 (and_5_out, stateE, comparator_10_eq);
  and and_6 (and_6_out, stateE, comparator_11_eq);
  and and_7 (and_7_out, stateB, or_4_out);
  not not_5 (not_5_out, ERET);
  not not_6 (not_6_out, j_type);
  and and_8 (and_8_out, not_7_out, stateA);
  and and_9 (and_9_out, and_4_out, not_3_out, not_4_out);
  and and_10 (and_10_out, and_7_out, not_5_out, not_6_out);
  and and_11 (and_11_out, stateB, j_type);
  // Probe on stateF
  // Probe on stateG
  // Probe on stateH
  // Probe on stateI
  // Probe on stateJ
  // Probe on rd_data1
  REG_FILE reg_file_1 (
    .wr_data(write_data_t), .wr_en(wr_en), .wr_reg(multiplexer_7_out), .rd_data1(rd_data1),
    .rd_data2(reg_file_1_rd_data2), .clk(clk), .rst(rst), .rd_reg1(_21_25), .rd_reg2(_16_20));
  Shifter #(.width(32)) shifter_1 (.in(imm_1), .\dist (5'b00010), .out(shifter_1_out));
  Comparator #(.width(6)) comparator_14 (.a(_31_26), .b({6{1'b0}}), .eq(comparator_14_eq));  // open: gt, lt
  D_Flip_Flop State_A (.clk(clk), .D(or_1_out), .Q(stateA), .preset(rst));  // open: Qn, en, reset
  not not_7 (not_7_out, ERET);
  D_Flip_Flop State_B (.clk(clk), .D(and_8_out), .Q(stateB), .reset(rst));  // open: Qn, preset, en
  D_Flip_Flop State_C (.clk(clk), .D(and_3_out), .Q(stateC), .reset(rst));  // open: Qn, preset, en
  D_Flip_Flop State_D (.clk(clk), .D(stateC), .Q(stateD), .reset(rst));  // open: Qn, preset, en
  Register #(.width(32)) A (.D(rd_data1), .en(1'b1), .Q(A_q), .clk(clk), .clr(rst));
  Register #(.width(32)) B (.D(reg_file_1_rd_data2), .en(1'b1), .Q(write_data), .clk(clk), .clr(rst));
  D_Flip_Flop State_E (.clk(clk), .D(and_9_out), .Q(stateE), .reset(rst));  // open: Qn, preset, en
  D_Flip_Flop State_F (.clk(clk), .D(and_5_out), .Q(stateF), .reset(rst));  // open: Qn, preset, en
  D_Flip_Flop State_G (.clk(clk), .D(and_6_out), .Q(stateG), .reset(rst));  // open: Qn, preset, en
  D_Flip_Flop State_H (.clk(clk), .D(stateG), .Q(stateH), .reset(rst));  // open: Qn, preset, en
  D_Flip_Flop State_I (.clk(clk), .D(and_10_out), .Q(stateI), .reset(rst));  // open: Qn, preset, en
  D_Flip_Flop State_J (.clk(clk), .D(and_11_out), .Q(stateJ), .reset(rst));  // open: Qn, preset, en
  Comparator #(.width(6)) comparator_15 (.a(_31_26), .b(6'b100011), .eq(comparator_15_eq));  // open: gt, lt
  Comparator #(.width(6)) comparator_16 (.a(_31_26), .b(6'b101011), .eq(comparator_16_eq));  // open: gt, lt
  Comparator #(.width(6)) comparator_17 (.a(_31_26), .b(6'b001100), .eq(comparator_17_eq));  // open: gt, lt
  Comparator #(.width(6)) comparator_18 (.a(_31_26), .b(6'b001101), .eq(comparator_18_eq));  // open: gt, lt
  Comparator #(.width(6)) comparator_19 (.a(_31_26), .b(6'b001110), .eq(comparator_19_eq));  // open: gt, lt
  Multiplexer #(.width(32), .enable("false")) multiplexer_10 (
    .in0(inst_addr), .in1(A_q), .out(multiplexer_10_out), .sel(sel_opA));
  or or_5 (or_5_out, comparator_15_eq, comparator_16_eq);
  or or_6 (bitwise_imm, comparator_17_eq, comparator_18_eq, comparator_19_eq);
  // Probe on PC_in
  // Probe on multiplexer_10_out
  Multiplexer #(.select(2), .width(32), .enable("false")) multiplexer_11 (
    .in0(write_data), .in1(32'h4), .in2(imm_1), .in3(shifter_1_out), .out(multiplexer_11_out),
    .sel(priority_encoder_1_out));
  Comparator #(.width(6)) comparator_20 (.a(_31_26), .b({6{1'b0}}), .eq(comparator_20_eq));  // open: gt, lt
  Comparator #(.width(6)) comparator_21 (.a(_31_26), .b({6{1'b0}}), .eq(comparator_21_eq));  // open: gt, lt
  not not_8 (not_8_out, comparator_21_eq);
  or or_7 (is_itype, or_5_out, bitwise_imm);
  and and_12 (and_12_out, comparator_20_eq, stateC);
  and and_13 (and_13_out, not_8_out, stateC);
  or or_8 (or_8_out, and_13_out, stateE);
  and and_14 (and_14_out, stateA, jal);
  Comparator #(.width(6)) comparator_22 (.a(_31_26), .b({6{1'b0}}), .eq(comparator_22_eq));  // open: gt, lt
  Multiplexer #(.select(2), .width(32), .enable("false")) multiplexer_12 (
    .in0(ALU_OUT), .in1(alu_res), .in2({inst_addr[31:28], target}), .in3(rd_data1), .out(PC_in), .sel(sel_PC));
  or or_9 (or_9_out, and_12_out, stateI);
  and and_15 (and_15_out, stateH, ~mp2board);  // AND_Gate
  or or_10 (wr_en1, and_14_out, stateD, stateH);
  or or_11 (or_11_out, stateA, stateB, stateE);
  and and_16 (and_16_out, stateG, mp2board);
  ALU alu_1 (
    .imm(imm_final), .shamt(_6_10), .op1(multiplexer_10_out), .op2(multiplexer_11_out), .zero_flag(zeroflag),
    .result(alu_res), .ALU_code(sel_alu));
  and and_17 (and_17_out, stateG, mp2board);
  or or_12 (or_12_out, stateC, stateE, stateI);
  not not_9 (not_9_out, or_13_out);
  or or_13 (or_13_out, stateA, stateB);
  Comparator #(.width(6)) comparator_23 (.a(_31_26), .b({6{1'b0}}), .eq(comparator_23_eq));  // open: gt, lt
  not not_10 (not_10_out, comparator_23_eq);
  Comparator #(.width(6)) comparator_24 (.a(_31_26), .b({6{1'b0}}), .eq(comparator_24_eq));  // open: gt, lt
  Comparator #(.width(6)) comparator_25 (.a(ALU_code), .b(6'b000100), .eq(comparator_25_eq));  // open: gt, lt
  Comparator #(.width(6)) comparator_26 (.a(ALU_code), .b(6'b000101), .eq(comparator_26_eq));  // open: gt, lt
  Comparator #(.width(6)) comparator_27 (.a(_0_5), .b(6'b001000), .eq(comparator_27_eq));  // open: gt, lt
  Comparator #(.width(6)) comparator_28 (.a(_31_26), .b({6{1'b0}}), .eq(comparator_28_eq));  // open: gt, lt
  Comparator #(.width(6), .mode("unsigned")) comparator_29 (.a(_31_26), .b(6'b000010), .eq(jump));  // open: gt, lt
  Comparator #(.width(6), .mode("unsigned")) comparator_30 (.a(_31_26), .b(6'b000011), .eq(jal));  // open: gt, lt
  Comparator #(.width(6)) comparator_31 (.a(_0_5), .b(6'b001000), .eq(comparator_31_eq));  // open: gt, lt
  and and_18 (jr, comparator_31_eq, comparator_22_eq);
  or or_14 (j_type, jump, jal, jr);
  // Probe on ALU_OUT
  Register #(.width(32)) u_ALU_out (.D(alu_res), .en(1'b1), .Q(ALU_OUT), .clk(clk), .clr(rst));
  Priority_Encoder #(.select(2)) priority_encoder_1 (
    .in0(or_9_out), .in1(stateA), .in2(or_8_out), .in3(stateB), .out(priority_encoder_1_out), .en_in(1'b1));  // open: gs, en_out
  or or_15 (or_15_out, stateD, and_15_out);
  or or_16 (wr_en, or_15_out, and_19_out, and_17_out);
  and and_19 (and_19_out, stateJ, jal);
  and and_20 (sel_opA, or_12_out, not_9_out);
  Priority_Encoder #(.select(2)) priority_encoder_2 (
    .in0(not_10_out), .in1(comparator_24_eq), .in2(or_11_out), .in3(stateI), .out(priority_encoder_2_out),
    .en_in(1'b1));  // open: gs, en_out
  Priority_Encoder #(.select(2)) priority_encoder_3 (
    .in0(stateH), .in1(stateD), .in2(stateJ), .in3(and_16_out), .out(sel_data), .en_in(1'b1));  // open: gs, en_out
  and and_21 (and_21_out, comparator_25_eq, zeroflag);
  and and_22 (and_22_out, comparator_26_eq, not_11_out);
  not not_11 (not_11_out, zeroflag);
  and and_23 (jr, comparator_27_eq, comparator_28_eq);
  and and_24 (r_type, ~comparator_27_eq, comparator_28_eq);  // AND_Gate
  Multiplexer #(.select(2), .width(6), .enable("false")) multiplexer_13 (
    .in0(_31_26), .in1(_0_5), .in2(6'b100000), .in3(6'b100010), .out(sel_alu), .sel(priority_encoder_2_out));
  or or_17 (branched, and_21_out, and_22_out);
  Shifter #(.width(32)) shifter_2 (
    .in({_31_26, _21_25, _16_20, _11_15, _6_10, _0_5}), .\dist (5'b00010), .out({shifter_2_out, target}));
  and and_25 (and_25_out, stateG, mp2board);
  and and_26 (and_26_out, stateI, branched);
  or or_18 (or_18_out, jump, jal);
  Comparator #(.width(6)) comparator_32 (.a(ALU_code), .b(6'b001000), .eq(comparator_32_eq));  // open: gt, lt
  Comparator #(.width(6)) comparator_33 (.a(_31_26), .b({6{1'b0}}), .eq(comparator_33_eq));  // open: gt, lt
  Comparator #(.width(6)) comparator_34 (.a(ALU_code), .b(6'b001010), .eq(comparator_34_eq));  // open: gt, lt
  Comparator #(.width(6)) comparator_35 (.a(ALU_code), .b(6'b001100), .eq(comparator_35_eq));  // open: gt, lt
  Comparator #(.width(6)) comparator_36 (.a(ALU_code), .b(6'b001101), .eq(comparator_36_eq));  // open: gt, lt
  Comparator #(.width(6)) comparator_37 (.a(ALU_code), .b(6'b001110), .eq(comparator_37_eq));  // open: gt, lt
  Comparator #(.width(6)) comparator_38 (.a(ALU_code), .b(6'b100011), .eq(comparator_38_eq));  // open: gt, lt
  Comparator #(.width(6)) comparator_39 (.a(ALU_code), .b(6'b101011), .eq(comparator_39_eq));  // open: gt, lt
  Comparator #(.width(6)) comparator_40 (.a(ALU_code), .b(6'b000100), .eq(comparator_40_eq));  // open: gt, lt
  Comparator #(.width(6)) comparator_41 (.a(ALU_code), .b(6'b000101), .eq(comparator_41_eq));  // open: gt, lt
  or or_19 (sel_IorD, stateG, stateF);
  or or_20 (or_20_out, int_signal, interrupt__from_device);
  and and_27 (and_27_out, stateJ, or_18_out);
  and and_28 (and_28_out, stateJ, jr);
  and and_29 (and_29_out, stateD, i_type);
  and and_30 (and_30_out, stateD, r_type);
  and and_31 (and_31_out, stateJ, jal);
  Comparator #(.width(32)) comparator_42 (
    .a(ALU_OUT), .b(32'h3000), .gt(comparator_42_gt), .eq(comparator_42_eq));  // open: lt
  or or_21 (wr_pc, stateA, stateJ, and_26_out);
  and and_32 (and_32_out, or_20_out, enable_int);
  Comparator #(.width(32), .mode("unsigned")) comparator_43 (
    .a(inst_addr), .b(32'h1000), .lt(enable_int));  // open: gt, eq
  Comparator #(.width(32), .mode("unsigned")) comparator_44 (
    .a(instruction), .b(32'h42000018), .eq(comparator_44_eq));  // open: gt, lt
  or or_22 (or_22_out, and_29_out, and_25_out, stateH);
  nand nand_1 (sel_isr, int_signal, stateA);
  or or_23 (or_23_out, comparator_42_gt, comparator_42_eq);
  Comparator #(.width(32)) comparator_45 (
    .a(ALU_OUT), .b(32'h3018), .eq(comparator_45_eq), .lt(comparator_45_lt));  // open: gt
  Register #(.width(1)) INT_Register (.D(and_32_out), .en(1'b1), .Q(int_signal), .clk(clk), .clr(rst));
  Priority_Encoder #(.select(2)) priority_encoder_4 (
    .in0(stateI), .in1(stateA), .in2(and_27_out), .in3(and_28_out), .out(sel_PC), .en_in(1'b1));  // open: gs, en_out
  and and_33 (ERET, comparator_44_eq, ~stateB);  // AND_Gate
  Priority_Encoder #(.select(2)) priority_encoder_5 (
    .in0(or_22_out), .in1(and_30_out), .in2(and_31_out), .out(sel_dest), .en_in(1'b1));  // open: in3, gs, en_out
  or or_24 (or_24_out, comparator_45_eq, comparator_45_lt);
  and and_34 (mp2board, or_23_out, or_24_out);
  or or_25 (or_25_out, comparator_32_eq, comparator_33_eq, comparator_34_eq, comparator_35_eq, comparator_36_eq, comparator_37_eq, comparator_38_eq, comparator_39_eq, comparator_40_eq, comparator_41_eq);
  not not_12 (NOP, or_25_out);

  assign data_addr = ALU_OUT;

  // Other names for the same wires on the sheet: inst[31:0] = {_31_26, _21_25, _16_20, _11_15, _6_10, _0_5};
  //   current_PC[31:0] = inst_addr; interrupt_from_device = interrupt__from_device; ret_isr = ERET;
  //   save_pc = int_signal; target[31:28] = inst_addr[31:28]; wr_data[31:0] = write_data; wr_ir = stateA

  // Notes on the sheet:
  //   lw
  //   sw
  //   sw
  //   lw
  //   PASTE YOUR PROCESSOR SCHEMATIC HERE AND CONNECT TO THE PINS. NO MODIFICATIONS ALLOWED TO THE PINS.
  //   beq
  //   bne
  //   sel_data
  //   rs
  //   op
  //   shamt
  //   func
  //   rs
  //   rt
  //   rd
  //   Arithmetic R
  //   lw
  //   sw
  //   andi
  //   ori
  //   xori
  //   Control Signals
  //   beq
  //   bne
  //   sel_opB
  //   aluout
  //   NOP
endmodule
