// Logisim project mp2_top.circ as structural Verilog: 3 circuits, main circuit MP2-TOP
module MP2_TOP (
  input  rst
);

  wire _1_2_out, _1_out, _2_2_out, _2_out, _3_2_out, _3_out, _4_2_out, _4_out, _5_2_out, _5_out,
       board_interface_1_irq, C_out, clk_out, mips_1_clk_2, N_out, score_interface_1_bottom1,
       score_interface_1_bottom2, score_interface_1_out_3, score_interface_1_out_4, score_interface_1_out_5,
       score_interface_1_out_7, score_interface_1_out_8, score_interface_1_out_9, score_interface_1_out_11,
       score_interface_1_out_12, score_interface_1_out_13, score_interface_1_out_15,
       score_interface_1_out_16, score_interface_1_out_17, score_interface_1_top1, score_interface_1_top2,
       slots_interface_1_b0, slots_interface_1_b1, slots_interface_2_b0, slots_interface_2_b1,
       slots_interface_3_b0, slots_interface_3_b1, slots_interface_4_b0, slots_interface_4_b1,
       slots_interface_5_b0, slots_interface_5_b1, slots_interface_6_b0, slots_interface_6_b1,
       slots_interface_7_b0, slots_interface_7_b1, slots_interface_8_b0, slots_interface_8_b1,
       slots_interface_9_b0, slots_interface_9_b1, slots_interface_10_b0, slots_interface_10_b1,
       slots_interface_11_b0, slots_interface_11_b1, slots_interface_12_b0, slots_interface_12_b1,
       slots_interface_13_b0, slots_interface_13_b1, slots_interface_14_b0, slots_interface_14_b1,
       slots_interface_15_b0, slots_interface_15_b1, slots_interface_16_b0, slots_interface_16_b1,
       slots_interface_17_b0, slots_interface_17_b1, slots_interface_18_b0, slots_interface_18_b1,
       slots_interface_19_b0, slots_interface_19_b1, slots_interface_20_b0, slots_interface_20_b1,
       slots_interface_21_b0, slots_interface_21_b1, slots_interface_22_b0, slots_interface_22_b1,
       slots_interface_23_b0, slots_interface_23_b1, slots_interface_24_b0, slots_interface_24_b1,
       slots_interface_25_b0, slots_interface_25_b1;
  wire [5:0] buttons_interconn_1_out, buttons_interconn_2_out;
  wire [9:0] board_interface_1__0x300c_2, board_interface_1__0x3004_2, board_interface_1__0x3008_2,
       board_interface_1__0x3010_2, board_interface_1__0x3014_2, slots_interface_6_input_2,
       slots_interface_7_input_2, slots_interface_8_input_2, slots_interface_9_input_2,
       slots_interface_10_input_2, slots_interface_11_input_2, slots_interface_12_input_2,
       slots_interface_13_input_2, slots_interface_14_input_2, slots_interface_15_input_2,
       slots_interface_16_input_2, slots_interface_17_input_2, slots_interface_18_input_2,
       slots_interface_19_input_2, slots_interface_20_input_2, slots_interface_21_input_2,
       slots_interface_22_input_2, slots_interface_23_input_2, slots_interface_24_input_2,
       slots_interface_25_input_2, wires1_1__0x300c_2, wires1_1__0x3004_2, wires1_1__0x3008_2,
       wires1_1__0x3010_2, wires1_1__0x3014_2;
  wire [16:0] board_interface_1__0x3018_2;
  wire [31:0] board_interface_1__0x3000, mips_1__0x300c, mips_1__0x3004, mips_1__0x3008, mips_1__0x3010,
       mips_1__0x3014, mips_1__0x3018;

  // pads_left_board pads_left_board_1: pin names not known
  slots_interface slots_interface_1 (
    .b1(slots_interface_1_b1), .\input (slots_interface_7_input_2), .b0(slots_interface_1_b0));  // open: input_2
  LED led_1 (.in(slots_interface_1_b0));
  LED led_2 (.in(slots_interface_1_b1));
  LED led_3 (.in(slots_interface_2_b0));
  LED led_4 (.in(slots_interface_2_b1));
  slots_interface slots_interface_2 (
    .b1(slots_interface_2_b1), .\input (slots_interface_8_input_2), .b0(slots_interface_2_b0));  // open: input_2
  LED led_5 (.in(slots_interface_3_b0));
  slots_interface slots_interface_3 (
    .b1(slots_interface_3_b1), .\input (slots_interface_10_input_2), .b0(slots_interface_3_b0));  // open: input_2
  LED led_6 (.in(slots_interface_3_b1));
  LED led_7 (.in(slots_interface_4_b0));
  LED led_8 (.in(slots_interface_4_b1));
  slots_interface slots_interface_4 (
    .b1(slots_interface_4_b1), .\input (slots_interface_13_input_2), .b0(slots_interface_4_b0));  // open: input_2
  LED led_9 (.in(slots_interface_5_b1));
  slots_interface slots_interface_5 (
    .b1(slots_interface_5_b1), .\input (slots_interface_14_input_2), .b0(slots_interface_5_b0));  // open: input_2
  LED led_10 (.in(slots_interface_5_b0));
  // pads_center_button pads_center_button_1: pin names not known
  Button _1 (.out(_1_out));
  // pads_left_button pads_left_button_1: pin names not known
  Button _1_2 (.out(_1_2_out));
  // pads_center_button pads_center_button_2: pin names not known
  // pads_left_button pads_left_button_2: pin names not known
  _7_Segment_Display u_7_segment_display_1 (
    .g(score_interface_1_top2), .f(score_interface_1_out_11), .a(score_interface_1_out_12),
    .b(score_interface_1_out_13), .e(score_interface_1_bottom2), .d(score_interface_1_out_15),
    .c(score_interface_1_out_16), .dp(score_interface_1_out_17));
  LED led_11 (.in(slots_interface_6_b1));
  slots_interface slots_interface_6 (
    .input_2(slots_interface_6_input_2), .b1(slots_interface_6_b1), .\input (slots_interface_17_input_2),
    .b0(slots_interface_6_b0));
  LED led_12 (.in(slots_interface_7_b0));
  LED led_13 (.in(slots_interface_7_b1));
  slots_interface slots_interface_7 (
    .input_2(slots_interface_7_input_2), .b1(slots_interface_7_b1), .\input (slots_interface_6_input_2),
    .b0(slots_interface_7_b0));
  LED led_14 (.in(slots_interface_6_b0));
  LED led_15 (.in(slots_interface_8_b0));
  LED led_16 (.in(slots_interface_8_b1));
  slots_interface slots_interface_8 (
    .input_2(slots_interface_8_input_2), .b1(slots_interface_8_b1), .\input (slots_interface_9_input_2),
    .b0(slots_interface_8_b0));
  slots_interface slots_interface_9 (
    .input_2(slots_interface_9_input_2), .b1(slots_interface_9_b1), .\input (slots_interface_18_input_2),
    .b0(slots_interface_9_b0));
  LED led_17 (.in(slots_interface_9_b1));
  LED led_18 (.in(slots_interface_9_b0));
  LED led_19 (.in(slots_interface_11_b1));
  slots_interface slots_interface_10 (
    .input_2(slots_interface_10_input_2), .b1(slots_interface_10_b1), .\input (slots_interface_11_input_2),
    .b0(slots_interface_10_b0));
  LED led_20 (.in(slots_interface_11_b0));
  LED led_21 (.in(slots_interface_10_b0));
  slots_interface slots_interface_11 (
    .input_2(slots_interface_11_input_2), .b1(slots_interface_11_b1), .\input (slots_interface_21_input_2),
    .b0(slots_interface_11_b0));
  LED led_22 (.in(slots_interface_10_b1));
  LED led_23 (.in(slots_interface_13_b1));
  LED led_24 (.in(slots_interface_13_b0));
  LED led_25 (.in(slots_interface_12_b0));
  slots_interface slots_interface_12 (
    .input_2(slots_interface_12_input_2), .b1(slots_interface_12_b1), .\input (slots_interface_22_input_2),
    .b0(slots_interface_12_b0));
  slots_interface slots_interface_13 (
    .input_2(slots_interface_13_input_2), .b1(slots_interface_13_b1), .\input (slots_interface_12_input_2),
    .b0(slots_interface_13_b0));
  LED led_26 (.in(slots_interface_12_b1));
  slots_interface slots_interface_14 (
    .input_2(slots_interface_14_input_2), .b1(slots_interface_14_b1), .\input (slots_interface_15_input_2),
    .b0(slots_interface_14_b0));
  LED led_27 (.in(slots_interface_14_b0));
  LED led_28 (.in(slots_interface_14_b1));
  LED led_29 (.in(slots_interface_15_b0));
  LED led_30 (.in(slots_interface_15_b1));
  slots_interface slots_interface_15 (
    .input_2(slots_interface_15_input_2), .b1(slots_interface_15_b1), .\input (slots_interface_24_input_2),
    .b0(slots_interface_15_b0));
  Button _3 (.out(_3_out));
  // pads_center_button pads_center_button_3: pin names not known
  // pads_center_button pads_center_button_4: pin names not known
  Button _2 (.out(_2_out));
  Button _3_2 (.out(_3_2_out));
  // pads_center_button pads_center_button_5: pin names not known
  Button _2_2 (.out(_2_2_out));
  // pads_center_button pads_center_button_6: pin names not known
  _7_Segment_Display u_7_segment_display_2 (
    .g(score_interface_1_top1), .f(score_interface_1_out_3), .a(score_interface_1_out_4),
    .b(score_interface_1_out_5), .e(score_interface_1_bottom1), .d(score_interface_1_out_7),
    .c(score_interface_1_out_8), .dp(score_interface_1_out_9));
  LED led_31 (.in(slots_interface_16_b0));
  slots_interface slots_interface_16 (
    .input_2(slots_interface_16_input_2), .b1(slots_interface_16_b1), .\input (wires1_1__0x3014_2),
    .b0(slots_interface_16_b0));
  LED led_32 (.in(slots_interface_17_b1));
  LED led_33 (.in(slots_interface_16_b1));
  slots_interface slots_interface_17 (
    .input_2(slots_interface_17_input_2), .b1(slots_interface_17_b1), .\input (slots_interface_16_input_2),
    .b0(slots_interface_17_b0));
  LED led_34 (.in(slots_interface_17_b0));
  LED led_35 (.in(slots_interface_19_b0));
  LED led_36 (.in(slots_interface_18_b1));
  LED led_37 (.in(slots_interface_18_b0));
  slots_interface slots_interface_18 (
    .input_2(slots_interface_18_input_2), .b1(slots_interface_18_b1), .\input (slots_interface_19_input_2),
    .b0(slots_interface_18_b0));
  slots_interface slots_interface_19 (
    .input_2(slots_interface_19_input_2), .b1(slots_interface_19_b1), .\input (wires1_1__0x3010_2),
    .b0(slots_interface_19_b0));
  LED led_38 (.in(slots_interface_19_b1));
  slots_interface slots_interface_20 (
    .input_2(slots_interface_20_input_2), .b1(slots_interface_20_b1), .\input (wires1_1__0x300c_2),
    .b0(slots_interface_20_b0));
  LED led_39 (.in(slots_interface_20_b1));
  LED led_40 (.in(slots_interface_21_b1));
  LED led_41 (.in(slots_interface_20_b0));
  slots_interface slots_interface_21 (
    .input_2(slots_interface_21_input_2), .b1(slots_interface_21_b1), .\input (slots_interface_20_input_2),
    .b0(slots_interface_21_b0));
  LED led_42 (.in(slots_interface_21_b0));
  LED led_43 (.in(slots_interface_23_b1));
  slots_interface slots_interface_22 (
    .input_2(slots_interface_22_input_2), .b1(slots_interface_22_b1), .\input (slots_interface_23_input_2),
    .b0(slots_interface_22_b0));
  LED led_44 (.in(slots_interface_23_b0));
  slots_interface slots_interface_23 (
    .input_2(slots_interface_23_input_2), .b1(slots_interface_23_b1), .\input (wires1_1__0x3008_2),
    .b0(slots_interface_23_b0));
  LED led_45 (.in(slots_interface_22_b0));
  LED led_46 (.in(slots_interface_22_b1));
  slots_interface slots_interface_24 (
    .input_2(slots_interface_24_input_2), .b1(slots_interface_24_b1), .\input (slots_interface_25_input_2),
    .b0(slots_interface_24_b0));
  LED led_47 (.in(slots_interface_24_b0));
  LED led_48 (.in(slots_interface_25_b0));
  LED led_49 (.in(slots_interface_25_b1));
  slots_interface slots_interface_25 (
    .input_2(slots_interface_25_input_2), .b1(slots_interface_25_b1), .\input (wires1_1__0x3004_2),
    .b0(slots_interface_25_b0));
  LED led_50 (.in(slots_interface_24_b1));
  // pads_center_button pads_center_button_7: pin names not known
  Button _5 (.out(_5_out));
  // pads_center_button pads_center_button_8: pin names not known
  Button _4 (.out(_4_out));
  // pads_center_button pads_center_button_9: pin names not known
  Button _5_2 (.out(_5_2_out));
  Button _4_2 (.out(_4_2_out));
  // pads_center_button pads_center_button_10: pin names not known
  board_interface board_interface_1 (
    ._0x3018_2(board_interface_1__0x3018_2), ._0x3014_2(board_interface_1__0x3014_2),
    ._0x3010_2(board_interface_1__0x3010_2), ._0x300C_2(board_interface_1__0x300c_2),
    ._0x3008_2(board_interface_1__0x3008_2), ._0x3004_2(board_interface_1__0x3004_2),
    .row1(buttons_interconn_1_out), .row2(buttons_interconn_2_out), ._0x3018(mips_1__0x3018),
    ._0x3014(mips_1__0x3014), ._0x3010(mips_1__0x3010), ._0x300C(mips_1__0x300c), ._0x3008(mips_1__0x3008),
    ._0x3004(mips_1__0x3004), ._0x3000(board_interface_1__0x3000), .irq(board_interface_1_irq),
    .clk(mips_1_clk_2));
  score_interface score_interface_1 (
    .IN(board_interface_1__0x3018_2), .Bottom1(score_interface_1_bottom1),
    .Bottom2(score_interface_1_bottom2), .out_7(score_interface_1_out_7), .out_15(score_interface_1_out_15),
    .out_8(score_interface_1_out_8), .out_16(score_interface_1_out_16), .out_9(score_interface_1_out_9),
    .out_17(score_interface_1_out_17), .Top1(score_interface_1_top1), .Top2(score_interface_1_top2),
    .out_3(score_interface_1_out_3), .out_11(score_interface_1_out_11), .out_4(score_interface_1_out_4),
    .out_12(score_interface_1_out_12), .out_5(score_interface_1_out_5), .out_13(score_interface_1_out_13));
  wires1 wires1_1 (
    ._0x3014_2(wires1_1__0x3014_2), ._0x3010_2(wires1_1__0x3010_2), ._0x300C_2(wires1_1__0x300c_2),
    ._0x3008_2(wires1_1__0x3008_2), ._0x3004_2(wires1_1__0x3004_2), ._0x3014(board_interface_1__0x3014_2),
    ._0x3010(board_interface_1__0x3010_2), ._0x300C(board_interface_1__0x300c_2),
    ._0x3008(board_interface_1__0x3008_2), ._0x3004(board_interface_1__0x3004_2));
  buttons_interconn buttons_interconn_1 (
    .out(buttons_interconn_1_out), ._0(_1_out), ._1(_2_out), ._2(_3_out), ._3(_4_out), ._4(_5_out), ._5(C_out));
  Button C (.out(C_out));
  buttons_interconn buttons_interconn_2 (
    .out(buttons_interconn_2_out), ._0(_1_2_out), ._1(_2_2_out), ._2(_3_2_out), ._3(_4_2_out), ._4(_5_2_out),
    ._5(N_out));
  Button N (.out(N_out));
  // pads_bottom_button pads_bottom_button_1: pin names not known
  MIPS mips_1 (
    .clk(clk_out), .rst(rst), .intr(board_interface_1_irq), ._0x3018(mips_1__0x3018),
    ._0x3014(mips_1__0x3014), ._0x3010(mips_1__0x3010), ._0x3000(board_interface_1__0x3000),
    .clk_2(mips_1_clk_2), ._0x300C(mips_1__0x300c), ._0x3008(mips_1__0x3008), ._0x3004(mips_1__0x3004));
  Clock clk (.out(clk_out));
endmodule

module MIPS (
  input  clk,
  input  rst,
  input  intr,
  input  [31:0] _0x3000,
  output [31:0] _0x3018,
  output clk_2,
  output [31:0] _0x3014,
  output [31:0] _0x3010,
  output [31:0] _0x300C,
  output [31:0] _0x3008,
  output [31:0] _0x3004
);

  // mips_main main_1: pin names not known; wires that end beside it: intr, clk, rst
  memory memory_1 (
    .clk(clk), .rst(rst), ._0x3000(_0x3000), ._0x3004(_0x3004), ._0x3018(_0x3018), ._0x3008(_0x3008),
    ._0x3014(_0x3014), ._0x3010(_0x3010), ._0x300c(_0x300C));  // open: inst_addr, inst_data, mem_wr, data_addr, data_wdata, data_rdata

  assign clk_2 = clk;
endmodule

module DEVICE_TEST (
  input  [31:0] _0x3018,
  input  [31:0] _0x3014,
  input  [31:0] _0x3010,
  input  [31:0] _0x300C,
  input  [31:0] _0x3008,
  input  [31:0] _0x3004,
  output [31:0] _0x3000,
  output irq
);

  wire _1_2_out, _1_out, _2_2_out, _2_out, _3_2_out, _3_out, _4_2_out, _4_out, _5_2_out, _5_out, C_out,
       clk_out, N_out, score_interface_1_bottom1, score_interface_1_bottom2, score_interface_1_out_3,
       score_interface_1_out_4, score_interface_1_out_5, score_interface_1_out_7, score_interface_1_out_8,
       score_interface_1_out_9, score_interface_1_out_11, score_interface_1_out_12, score_interface_1_out_13,
       score_interface_1_out_15, score_interface_1_out_16, score_interface_1_out_17, score_interface_1_top1,
       score_interface_1_top2, slots_interface_1_b0, slots_interface_1_b1, slots_interface_2_b0,
       slots_interface_2_b1, slots_interface_3_b0, slots_interface_3_b1, slots_interface_4_b0,
       slots_interface_4_b1, slots_interface_5_b0, slots_interface_5_b1, slots_interface_6_b0,
       slots_interface_6_b1, slots_interface_7_b0, slots_interface_7_b1, slots_interface_8_b0,
       slots_interface_8_b1, slots_interface_9_b0, slots_interface_9_b1, slots_interface_10_b0,
       slots_interface_10_b1, slots_interface_11_b0, slots_interface_11_b1, slots_interface_12_b0,
       slots_interface_12_b1, slots_interface_13_b0, slots_interface_13_b1, slots_interface_14_b0,
       slots_interface_14_b1, slots_interface_15_b0, slots_interface_15_b1, slots_interface_16_b0,
       slots_interface_16_b1, slots_interface_17_b0, slots_interface_17_b1, slots_interface_18_b0,
       slots_interface_18_b1, slots_interface_19_b0, slots_interface_19_b1, slots_interface_20_b0,
       slots_interface_20_b1, slots_interface_21_b0, slots_interface_21_b1, slots_interface_22_b0,
       slots_interface_22_b1, slots_interface_23_b0, slots_interface_23_b1, slots_interface_24_b0,
       slots_interface_24_b1, slots_interface_25_b0, slots_interface_25_b1;
  wire [5:0] buttons_interconn_1_out, buttons_interconn_2_out;
  wire [9:0] board_interface_1__0x300c_2, board_interface_1__0x3004_2, board_interface_1__0x3008_2,
       board_interface_1__0x3010_2, board_interface_1__0x3014_2, slots_interface_6_input_2,
       slots_interface_7_input_2, slots_interface_8_input_2, slots_interface_9_input_2,
       slots_interface_10_input_2, slots_interface_11_input_2, slots_interface_12_input_2,
       slots_interface_13_input_2, slots_interface_14_input_2, slots_interface_15_input_2,
       slots_interface_16_input_2, slots_interface_17_input_2, slots_interface_18_input_2,
       slots_interface_19_input_2, slots_interface_20_input_2, slots_interface_21_input_2,
       slots_interface_22_input_2, slots_interface_23_input_2, slots_interface_24_input_2,
       slots_interface_25_input_2, wires1_1__0x300c_2, wires1_1__0x3004_2, wires1_1__0x3008_2,
       wires1_1__0x3010_2, wires1_1__0x3014_2;
  wire [16:0] board_interface_1__0x3018_2;

  // pads_left_board pads_left_board_1: pin names not known
  slots_interface slots_interface_1 (
    .b1(slots_interface_1_b1), .\input (slots_interface_6_input_2), .b0(slots_interface_1_b0));  // open: input_2
  LED led_1 (.in(slots_interface_1_b1));
  LED led_2 (.in(slots_interface_1_b0));
  LED led_3 (.in(slots_interface_2_b1));
  LED led_4 (.in(slots_interface_2_b0));
  slots_interface slots_interface_2 (
    .b1(slots_interface_2_b1), .\input (slots_interface_9_input_2), .b0(slots_interface_2_b0));  // open: input_2
  slots_interface slots_interface_3 (
    .b1(slots_interface_3_b1), .\input (slots_interface_11_input_2), .b0(slots_interface_3_b0));  // open: input_2
  LED led_5 (.in(slots_interface_3_b1));
  LED led_6 (.in(slots_interface_3_b0));
  slots_interface slots_interface_4 (
    .b1(slots_interface_4_b1), .\input (slots_interface_13_input_2), .b0(slots_interface_4_b0));  // open: input_2
  LED led_7 (.in(slots_interface_4_b0));
  LED led_8 (.in(slots_interface_4_b1));
  slots_interface slots_interface_5 (
    .b1(slots_interface_5_b1), .\input (slots_interface_14_input_2), .b0(slots_interface_5_b0));  // open: input_2
  LED led_9 (.in(slots_interface_5_b1));
  LED led_10 (.in(slots_interface_5_b0));
  // pads_center_button pads_center_button_1: pin names not known
  Button _1 (.out(_1_out));
  // pads_left_button pads_left_button_1: pin names not known
  // pads_left_button pads_left_button_2: pin names not known
  // pads_center_button pads_center_button_2: pin names not known
  Button _1_2 (.out(_1_2_out));
  _7_Segment_Display u_7_segment_display_1 (
    .g(score_interface_1_top2), .f(score_interface_1_out_11), .a(score_interface_1_out_12),
    .b(score_interface_1_out_13), .e(score_interface_1_bottom2), .d(score_interface_1_out_15),
    .c(score_interface_1_out_16), .dp(score_interface_1_out_17));
  LED led_11 (.in(slots_interface_7_b1));
  slots_interface slots_interface_6 (
    .input_2(slots_interface_6_input_2), .b1(slots_interface_6_b1), .\input (slots_interface_7_input_2),
    .b0(slots_interface_6_b0));
  LED led_12 (.in(slots_interface_6_b1));
  LED led_13 (.in(slots_interface_7_b0));
  LED led_14 (.in(slots_interface_6_b0));
  slots_interface slots_interface_7 (
    .input_2(slots_interface_7_input_2), .b1(slots_interface_7_b1), .\input (slots_interface_17_input_2),
    .b0(slots_interface_7_b0));
  LED led_15 (.in(slots_interface_9_b1));
  slots_interface slots_interface_8 (
    .input_2(slots_interface_8_input_2), .b1(slots_interface_8_b1), .\input (slots_interface_18_input_2),
    .b0(slots_interface_8_b0));
  LED led_16 (.in(slots_interface_9_b0));
  LED led_17 (.in(slots_interface_8_b1));
  slots_interface slots_interface_9 (
    .input_2(slots_interface_9_input_2), .b1(slots_interface_9_b1), .\input (slots_interface_8_input_2),
    .b0(slots_interface_9_b0));
  LED led_18 (.in(slots_interface_8_b0));
  slots_interface slots_interface_10 (
    .input_2(slots_interface_10_input_2), .b1(slots_interface_10_b1), .\input (slots_interface_21_input_2),
    .b0(slots_interface_10_b0));
  LED led_19 (.in(slots_interface_10_b0));
  LED led_20 (.in(slots_interface_10_b1));
  LED led_21 (.in(slots_interface_11_b0));
  slots_interface slots_interface_11 (
    .input_2(slots_interface_11_input_2), .b1(slots_interface_11_b1), .\input (slots_interface_10_input_2),
    .b0(slots_interface_11_b0));
  LED led_22 (.in(slots_interface_11_b1));
  LED led_23 (.in(slots_interface_12_b0));
  slots_interface slots_interface_12 (
    .input_2(slots_interface_12_input_2), .b1(slots_interface_12_b1), .\input (slots_interface_22_input_2),
    .b0(slots_interface_12_b0));
  LED led_24 (.in(slots_interface_13_b1));
  slots_interface slots_interface_13 (
    .input_2(slots_interface_13_input_2), .b1(slots_interface_13_b1), .\input (slots_interface_12_input_2),
    .b0(slots_interface_13_b0));
  LED led_25 (.in(slots_interface_13_b0));
  LED led_26 (.in(slots_interface_12_b1));
  LED led_27 (.in(slots_interface_14_b1));
  slots_interface slots_interface_14 (
    .input_2(slots_interface_14_input_2), .b1(slots_interface_14_b1), .\input (slots_interface_15_input_2),
    .b0(slots_interface_14_b0));
  LED led_28 (.in(slots_interface_15_b0));
  slots_interface slots_interface_15 (
    .input_2(slots_interface_15_input_2), .b1(slots_interface_15_b1), .\input (slots_interface_24_input_2),
    .b0(slots_interface_15_b0));
  LED led_29 (.in(slots_interface_15_b1));
  LED led_30 (.in(slots_interface_14_b0));
  // pads_center_button pads_center_button_3: pin names not known
  Button _2 (.out(_2_out));
  // pads_center_button pads_center_button_4: pin names not known
  Button _3 (.out(_3_out));
  Button _2_2 (.out(_2_2_out));
  // pads_center_button pads_center_button_5: pin names not known
  // pads_center_button pads_center_button_6: pin names not known
  Button _3_2 (.out(_3_2_out));
  _7_Segment_Display u_7_segment_display_2 (
    .g(score_interface_1_top1), .f(score_interface_1_out_3), .a(score_interface_1_out_4),
    .b(score_interface_1_out_5), .e(score_interface_1_bottom1), .d(score_interface_1_out_7),
    .c(score_interface_1_out_8), .dp(score_interface_1_out_9));
  LED led_31 (.in(slots_interface_16_b0));
  slots_interface slots_interface_16 (
    .input_2(slots_interface_16_input_2), .b1(slots_interface_16_b1), .\input (wires1_1__0x3014_2),
    .b0(slots_interface_16_b0));
  slots_interface slots_interface_17 (
    .input_2(slots_interface_17_input_2), .b1(slots_interface_17_b1), .\input (slots_interface_16_input_2),
    .b0(slots_interface_17_b0));
  LED led_32 (.in(slots_interface_16_b1));
  LED led_33 (.in(slots_interface_17_b0));
  LED led_34 (.in(slots_interface_17_b1));
  LED led_35 (.in(slots_interface_18_b1));
  LED led_36 (.in(slots_interface_19_b1));
  LED led_37 (.in(slots_interface_19_b0));
  slots_interface slots_interface_18 (
    .input_2(slots_interface_18_input_2), .b1(slots_interface_18_b1), .\input (slots_interface_19_input_2),
    .b0(slots_interface_18_b0));
  slots_interface slots_interface_19 (
    .input_2(slots_interface_19_input_2), .b1(slots_interface_19_b1), .\input (wires1_1__0x3010_2),
    .b0(slots_interface_19_b0));
  LED led_38 (.in(slots_interface_18_b0));
  LED led_39 (.in(slots_interface_21_b0));
  LED led_40 (.in(slots_interface_20_b1));
  LED led_41 (.in(slots_interface_20_b0));
  slots_interface slots_interface_20 (
    .input_2(slots_interface_20_input_2), .b1(slots_interface_20_b1), .\input (wires1_1__0x300c_2),
    .b0(slots_interface_20_b0));
  LED led_42 (.in(slots_interface_21_b1));
  slots_interface slots_interface_21 (
    .input_2(slots_interface_21_input_2), .b1(slots_interface_21_b1), .\input (slots_interface_20_input_2),
    .b0(slots_interface_21_b0));
  LED led_43 (.in(slots_interface_22_b1));
  LED led_44 (.in(slots_interface_23_b0));
  LED led_45 (.in(slots_interface_22_b0));
  slots_interface slots_interface_22 (
    .input_2(slots_interface_22_input_2), .b1(slots_interface_22_b1), .\input (slots_interface_23_input_2),
    .b0(slots_interface_22_b0));
  LED led_46 (.in(slots_interface_23_b1));
  slots_interface slots_interface_23 (
    .input_2(slots_interface_23_input_2), .b1(slots_interface_23_b1), .\input (wires1_1__0x3008_2),
    .b0(slots_interface_23_b0));
  LED led_47 (.in(slots_interface_24_b0));
  LED led_48 (.in(slots_interface_25_b1));
  slots_interface slots_interface_24 (
    .input_2(slots_interface_24_input_2), .b1(slots_interface_24_b1), .\input (slots_interface_25_input_2),
    .b0(slots_interface_24_b0));
  LED led_49 (.in(slots_interface_24_b1));
  LED led_50 (.in(slots_interface_25_b0));
  slots_interface slots_interface_25 (
    .input_2(slots_interface_25_input_2), .b1(slots_interface_25_b1), .\input (wires1_1__0x3004_2),
    .b0(slots_interface_25_b0));
  // pads_center_button pads_center_button_7: pin names not known
  Button _5 (.out(_5_out));
  // pads_center_button pads_center_button_8: pin names not known
  Button _4 (.out(_4_out));
  Button _4_2 (.out(_4_2_out));
  // pads_center_button pads_center_button_9: pin names not known
  // pads_center_button pads_center_button_10: pin names not known
  Button _5_2 (.out(_5_2_out));
  board_interface board_interface_1 (
    ._0x3018_2(board_interface_1__0x3018_2), ._0x3014_2(board_interface_1__0x3014_2),
    ._0x3010_2(board_interface_1__0x3010_2), ._0x300C_2(board_interface_1__0x300c_2),
    ._0x3008_2(board_interface_1__0x3008_2), ._0x3004_2(board_interface_1__0x3004_2),
    .row1(buttons_interconn_1_out), .row2(buttons_interconn_2_out), ._0x3018(_0x3018), ._0x3014(_0x3014),
    ._0x3010(_0x3010), ._0x300C(_0x300C), ._0x3008(_0x3008), ._0x3004(_0x3004), ._0x3000(_0x3000), .irq(irq),
    .clk(clk_out));
  score_interface score_interface_1 (
    .IN(board_interface_1__0x3018_2), .Bottom1(score_interface_1_bottom1),
    .Bottom2(score_interface_1_bottom2), .out_7(score_interface_1_out_7), .out_15(score_interface_1_out_15),
    .out_8(score_interface_1_out_8), .out_16(score_interface_1_out_16), .out_9(score_interface_1_out_9),
    .out_17(score_interface_1_out_17), .Top1(score_interface_1_top1), .Top2(score_interface_1_top2),
    .out_3(score_interface_1_out_3), .out_11(score_interface_1_out_11), .out_4(score_interface_1_out_4),
    .out_12(score_interface_1_out_12), .out_5(score_interface_1_out_5), .out_13(score_interface_1_out_13));
  wires1 wires1_1 (
    ._0x3014_2(wires1_1__0x3014_2), ._0x3010_2(wires1_1__0x3010_2), ._0x300C_2(wires1_1__0x300c_2),
    ._0x3008_2(wires1_1__0x3008_2), ._0x3004_2(wires1_1__0x3004_2), ._0x3014(board_interface_1__0x3014_2),
    ._0x3010(board_interface_1__0x3010_2), ._0x300C(board_interface_1__0x300c_2),
    ._0x3008(board_interface_1__0x3008_2), ._0x3004(board_interface_1__0x3004_2));
  buttons_interconn buttons_interconn_1 (
    .out(buttons_interconn_1_out), ._0(_1_out), ._1(_2_out), ._2(_3_out), ._3(_4_out), ._4(_5_out), ._5(C_out));
  Button C (.out(C_out));
  buttons_interconn buttons_interconn_2 (
    .out(buttons_interconn_2_out), ._0(_1_2_out), ._1(_2_2_out), ._2(_3_2_out), ._3(_4_2_out), ._4(_5_2_out),
    ._5(N_out));
  Button N (.out(N_out));
  // pads_bottom_button pads_bottom_button_1: pin names not known
  Clock clk (.out(clk_out));
endmodule
